// Digital circuit part_c.dig as structural Verilog
module part_c (
  input  in_0,
  input  in_1,
  input  in_2,
  output out_0
);

  wire fgnfet_1_s, fgpfet_1_d, fgpfet_3_d, fgpfet_4_d, nfet_5_s, nfet_6_s, nfet_17_d, pfet_1_d, pfet_2_d,
       pfet_3_d, pfet_4_d, pfet_5_d, pfet_6_d, pfet_9_d, pfet_10_d, pfet_11_d, pfet_12_d, pfet_13_d,
       pfet_14_d, pfet_15_d, pfet_16_d;

  PFET pfet_1 (.G(in_2), .S(1'b1), .D(pfet_1_d));
  NFET nfet_1 (.G(in_2), .D(pfet_1_d), .S(1'b0));
  PFET pfet_2 (.G(in_0), .S(1'b1), .D(pfet_2_d));
  NFET nfet_2 (.G(in_0), .D(pfet_2_d), .S(1'b0));
  FGPFET fgpfet_1 (.G(in_0), .S(1'b1), .D(fgpfet_1_d));
  FGNFET fgnfet_1 (.G(in_2), .D(fgpfet_1_d), .S(fgnfet_1_s));
  FGNFET fgnfet_2 (.G(in_0), .D(fgnfet_1_s), .S(1'b0));
  PFET pfet_3 (.G(in_1), .S(1'b1), .D(pfet_3_d));
  NFET nfet_3 (.G(in_1), .D(pfet_3_d), .S(1'b0));
  PFET pfet_4 (.G(in_2), .S(1'b1), .D(pfet_4_d));
  NFET nfet_4 (.G(in_2), .D(pfet_4_d), .S(1'b0));
  FGPFET fgpfet_2 (.G(in_2), .S(1'b1), .D(fgpfet_1_d));
  PFET pfet_5 (.G(pfet_4_d), .S(1'b1), .D(pfet_5_d));
  PFET pfet_6 (.G(pfet_2_d), .S(1'b1), .D(pfet_6_d));
  PFET pfet_7 (.G(pfet_1_d), .S(1'b1), .D(pfet_6_d));
  NFET nfet_5 (.G(pfet_2_d), .D(pfet_6_d), .S(nfet_5_s));
  PFET pfet_8 (.G(pfet_3_d), .S(1'b1), .D(pfet_5_d));
  NFET nfet_6 (.G(pfet_3_d), .D(pfet_5_d), .S(nfet_6_s));
  NFET nfet_7 (.G(pfet_4_d), .D(nfet_6_s), .S(1'b0));
  PFET pfet_9 (.G(fgpfet_1_d), .S(1'b1), .D(pfet_9_d));
  NFET nfet_8 (.G(fgpfet_1_d), .D(pfet_9_d), .S(1'b0));
  NFET nfet_9 (.G(pfet_1_d), .D(nfet_5_s), .S(1'b0));
  FGPFET fgpfet_3 (.G(pfet_6_d), .S(1'b1), .D(fgpfet_3_d));
  NFET nfet_10 (.G(pfet_6_d), .D(fgpfet_3_d), .S(1'b0));
  PFET pfet_10 (.G(pfet_5_d), .S(1'b1), .D(pfet_10_d));
  NFET nfet_11 (.G(pfet_5_d), .D(pfet_10_d), .S(1'b0));
  PFET pfet_11 (.G(pfet_9_d), .S(1'b1), .D(pfet_11_d));
  PFET pfet_12 (.G(fgpfet_3_d), .S(pfet_11_d), .D(pfet_12_d));
  PFET pfet_13 (.G(pfet_10_d), .S(1'b1), .D(pfet_13_d));
  PFET pfet_14 (.G(pfet_9_d), .S(pfet_13_d), .D(pfet_14_d));
  NFET nfet_12 (.G(pfet_9_d), .D(pfet_14_d), .S(1'b0));
  NFET nfet_13 (.G(pfet_9_d), .D(pfet_12_d), .S(1'b0));
  NFET nfet_14 (.G(fgpfet_3_d), .D(pfet_12_d), .S(1'b0));
  NFET nfet_15 (.G(pfet_10_d), .D(pfet_14_d), .S(1'b0));
  PFET pfet_15 (.G(pfet_12_d), .S(1'b1), .D(pfet_15_d));
  FGNFET fgnfet_3 (.G(pfet_12_d), .D(pfet_15_d), .S(1'b0));
  FGPFET fgpfet_4 (.G(pfet_14_d), .S(1'b1), .D(fgpfet_4_d));
  NFET nfet_16 (.G(pfet_14_d), .D(fgpfet_4_d), .S(1'b0));
  NFET nfet_17 (.G(fgpfet_4_d), .D(nfet_17_d), .S(1'b0));
  PFET pfet_16 (.G(fgpfet_4_d), .S(1'b1), .D(pfet_16_d));
  PFET pfet_17 (.G(pfet_15_d), .S(pfet_16_d), .D(nfet_17_d));
  NFET nfet_18 (.G(pfet_15_d), .D(nfet_17_d), .S(1'b0));
  PFET pfet_18 (.G(nfet_17_d), .S(1'b1), .D(out_0));
  NFET nfet_19 (.G(nfet_17_d), .D(out_0), .S(1'b0));
endmodule
